# Fritzing sketch ESP32-S3DK-I2CTest (saved by Fritzing 0.9.5d)
breadboards: 2

parts:
  ESP32-S3-DEVKIT1 = ESP32-S3-DEVKIT [part_number=ESP32-S3-DEVKIT]
  Universal_LCC_Node_Breakout1 = UniversalLCCNodeBreakout
  R1 = Resistor [tolerance=±5% resistance=2.2k package=THT]
  R2 = Resistor [tolerance=±5% resistance=2.2k package=THT]
  Part1 = 16-Channel 12-bit PWM Servo Driver - I2C [part_number=815]
  IC1 = MCP23017 [package="DIP (Dual Inline) [THT]"]
  R3 = Resistor [tolerance=±5% resistance=10k package=THT]

nets:
  3.3V: ESP32-S3-DEVKIT1.connector6, ESP32-S3-DEVKIT1.connector7, Universal_LCC_Node_Breakout1.connector1, R1.Pin_0, R2.Pin_0, Part1.VCC, IC1.Vdd, R3.Pin_1
  CAN RX: ESP32-S3-DEVKIT1.connector9, Universal_LCC_Node_Breakout1.connector2
  CAN TX: ESP32-S3-DEVKIT1.connector10, Universal_LCC_Node_Breakout1.connector3
  SDA: ESP32-S3-DEVKIT1.connector11, R1.Pin_1, Part1.SDA, IC1.SDA
  SCL: ESP32-S3-DEVKIT1.connector12, R2.Pin_1, Part1.SCL, IC1.SCL
  5V: ESP32-S3-DEVKIT1.connector26, Universal_LCC_Node_Breakout1.connector0, Part1.5.0V
  GND: ESP32-S3-DEVKIT1.connector27, ESP32-S3-DEVKIT1.connector28, ESP32-S3-DEVKIT1.connector29, ESP32-S3-DEVKIT1.connector49, Universal_LCC_Node_Breakout1.connector4, Part1.GND, Part1.OE, IC1.Vss, IC1.A0, IC1.A1, IC1.A2
  N1: IC1.~RESET, R3.Pin_0

custom parts:
  16-Channel 12-bit PWM Servo Driver - I2C: You want to make a cool robot, maybe a hexapod walker, or maybe just a piece of art with a lot of moving parts. Or maybe you want to drive a lot of LEDs with precise PWM output. Using only two pins, control 16 free-running PWM outputs! You can even chain up 62 breakouts to control up to 992 PWM outputs.
  MCP23017: MCP23017 -- GPIO Port expander
