# Fritzing sketch ESP32-S3-TextDisplaySign (saved by Fritzing 0.9.6b)

parts:
  proto1 = Adafruit_Permaproto_Full_sized_Board
  ESP32-S3-DEVKIT1 = ESP32-S3-DEVKIT [part_number=ESP32-S3-DEVKIT]
  Part1 = TFT 1.8 inch 160x128 w microSD [part_number=358]
  J2 = female pin header, 5 pins [form="♀ (female)"]
  J3 = male pin header, 10 pins [form="♂ (male)"]
  J4 = female pin header, 10 pins [form="♀ (female)"]
  Universal_LCC_Node_Breakout1 = UniversalLCCNodeBreakout
  J5 = male pin header, 5 pins [form="♂ (male)"]

nets:
  N1: proto1.connectorA1, proto1.connectorA2, proto1.connectorF35
  N2: proto1.connectorA4, proto1.connectorF36
  N3: proto1.connectorA5, proto1.connectorF37
  N4: proto1.connectorA11, proto1.connectorA55
  N5: proto1.connectorA14, proto1.connectorA54
  N6: proto1.connectorA15, proto1.connectorA58
  N7: proto1.connectorA16, proto1.connectorA56
  N8: proto1.connectorA19, proto1.connectorA51
  N9: proto1.connectorA21, proto1.connectorF34
  N10: proto1.connectorA22, proto1.connectorX22
  N11: proto1.connectorA49, proto1.connectorX49
  N12: proto1.connectorA50, proto1.connectorG34
  N13: proto1.connectorA52, proto1.connectorH16
  N14: proto1.connectorA53, proto1.connectorH17
  N15: proto1.connectorA57, proto1.connectorH10
  N16: proto1.connectorC1, proto1.connectorW1
  N17: proto1.connectorH21, proto1.connectorZ21
  N18: proto1.connectorH22, proto1.connectorZ22
  N19: proto1.connectorJ38, proto1.connectorZ38
  N20: proto1.connectorW59, proto1.connectorY59
  N21: proto1.connectorX60, proto1.connectorZ60
  3.3V: ESP32-S3-DEVKIT1.connector6, ESP32-S3-DEVKIT1.connector7, J2.pin2
  CAN_RX: ESP32-S3-DEVKIT1.connector9, J2.pin3
  CAN_TX: ESP32-S3-DEVKIT1.connector10, J2.pin4
  MOSI: ESP32-S3-DEVKIT1.connector16, J4.pin7
  DCS1: ESP32-S3-DEVKIT1.connector19, J4.pin6
  Backlight: ESP32-S3-DEVKIT1.connector20, J4.pin10
  SCLK: ESP32-S3-DEVKIT1.connector21, J4.pin8
  RST: ESP32-S3-DEVKIT1.connector24, J4.pin3
  5V: ESP32-S3-DEVKIT1.connector26, J2.pin1, J4.pin2
  GND: ESP32-S3-DEVKIT1.connector27, ESP32-S3-DEVKIT1.connector28, ESP32-S3-DEVKIT1.connector29, J2.pin5, J4.pin1
  CardCS: ESP32-S3-DEVKIT1.connector33, J4.pin5
  DRs: ESP32-S3-DEVKIT1.connector34, J4.pin4
  MISO: ESP32-S3-DEVKIT1.connector40, J4.pin9
  N22: Part1.LITE, J3.pin10
  N23: Part1.MISO, J3.pin9
  N24: Part1.SCLK, J3.pin8
  N25: Part1.MOSI, J3.pin7
  N26: Part1.TFTCS, J3.pin6
  N27: Part1.CARDCS, J3.pin5
  N28: Part1.TFTDC, J3.pin4
  N29: Part1.RESET, J3.pin3
  N30: Part1.+5V, J3.pin2
  N31: Part1.GND, J3.pin1
  N32: Universal_LCC_Node_Breakout1.connector0, J5.pin1
  N33: Universal_LCC_Node_Breakout1.connector1, J5.pin2
  N34: Universal_LCC_Node_Breakout1.connector2, J5.pin3
  N35: Universal_LCC_Node_Breakout1.connector3, J5.pin4
  N36: Universal_LCC_Node_Breakout1.connector4, J5.pin5

custom parts:
  TFT 1.8 inch 160x128 w microSD: This lovely little display breakout is the best way to add a small, colorful and bright display to any project. Since the display uses 4-wire SPI to communicate and has its own pixel-addressable frame buffer, it can be used with every kind of microcontroller. Even a very small one with low memory and few pins available! The 1.8" display has 128x160 color pixels.
